// Logisim project Logisim.circ as structural Verilog: 1 circuit, main circuit main
module main (
  input  in_1,
  input  in_2,
  input  in_3,
  input  in_4
);

  wire t_ff_1_q, t_ff_2_qn, t_ff_3_q, t_ff_4_qn, t_ff_5_q, t_ff_6_qn, t_ff_7_q, t_ff_8_qn;

  D_Flip_Flop d_ff_1 ();  // open: D, clk, Q, Qn, preset, reset
  T_Flip_Flop t_ff_1 (.T(in_1), .clk(in_2), .Q(t_ff_1_q));  // open: Qn, reset, preset
  T_Flip_Flop t_ff_2 (.T(in_3), .clk(in_4), .Qn(t_ff_2_qn));  // open: Q, reset, preset
  T_Flip_Flop t_ff_3 (.T(in_1), .clk(t_ff_1_q), .Q(t_ff_3_q));  // open: Qn, reset, preset
  T_Flip_Flop t_ff_4 (.T(in_3), .clk(t_ff_2_qn), .Qn(t_ff_4_qn));  // open: Q, reset, preset
  T_Flip_Flop t_ff_5 (.T(in_1), .clk(t_ff_3_q), .Q(t_ff_5_q));  // open: Qn, reset, preset
  T_Flip_Flop t_ff_6 (.T(in_3), .clk(t_ff_4_qn), .Qn(t_ff_6_qn));  // open: Q, reset, preset
  T_Flip_Flop t_ff_7 (.T(in_1), .clk(t_ff_5_q), .Q(t_ff_7_q));  // open: Qn, reset, preset
  T_Flip_Flop t_ff_8 (.T(in_3), .clk(t_ff_6_qn), .Qn(t_ff_8_qn));  // open: Q, reset, preset
  T_Flip_Flop t_ff_9 (.T(in_1), .clk(t_ff_7_q));  // open: Q, Qn, reset, preset
  T_Flip_Flop t_ff_10 (.T(in_3), .clk(t_ff_8_qn));  // open: Q, Qn, reset, preset
endmodule
